# Fritzing sketch 01 (saved by Fritzing 0.9.2b)
perfboards: 1
breadboards: 1

parts:
  Q1 = Basic FET P-Channel [package="TO220 [THT]"]
  R1 = Resistor [tolerance=±5% resistance=1k package=THT]
  J1 = Screw terminal - 2 pins [package=THT]
  J2 = Screw terminal - 2 pins [package=THT]

nets:
  N1: Q1.gate, R1.Pin_0
  N2: Q1.drain, J1.pin1
  N3: Q1.source, J1.pin2, J2.pin1
  N4: R1.Pin_1, J2.pin2

notes:
  fixture ground line
  arduino ground
  arduino PWM signal
